# Fritzing sketch motor_controller (saved by Fritzing 0.9.4)
breadboards: 2

parts:
  Part1 = Arduino Mega ADK (Rev3)
  Part4 = Adafruit Motor/Stepper/Servo Shield [part_number="Adafruit #1438"]
  HC-SR04_Sensor_1 = HC-SR04 Ultrasonic Distance Sensor
  Part5 = InvenSense MPU6050
  Part6 = BlueSMiRF Silver [part_number=10269]
  VCC1 = Battery
  LED1 = LED - 3mm [color="Yellow (595nm)" package="3 mm [THT]"]
  LED2 = LED - 3mm [color="Green (555nm)" package="3 mm [THT]"]
  LED3 = LED - 3mm [color="Red (633nm)" package="3 mm [THT]"]
  R1 = Resistor [tolerance=±5% resistance=220 package="2010 [SMD]"]
  R2 = Resistor [tolerance=±5% resistance=220 package="2010 [SMD]"]
  R3 = Resistor [tolerance=±5% resistance=220 package="2010 [SMD]"]
  MCU1 = Raspberry Pi Zero  # not connected
  Part8 = Adafruit 4-channel I2C-safe Bi-directional Logic Level Converter [part_number="Adafruit #757"]
  Part9 = Adafruit Pi Cobbler Plus [part_number="Adafruit #2029"]  # not connected
  Part7 = Adafruit 4-channel I2C-safe Bi-directional Logic Level Converter [part_number="Adafruit #757"]
  S1 = Toggle Switch [package=THT]
  M1 = DC Motor
  M2 = DC Motor
  M3 = DC Motor
  M4 = DC Motor

nets:
  N1: Part1.D19/RX1, Part6.TX_5V
  N2: Part1.D18/TX1, Part6.RX_5V
  N3: Part1.D17/RX2, Part7.B3
  N4: Part1.D16/TX2, Part7.B4
  N5: Part1.D22, HC-SR04_Sensor_1.TRIG
  N6: Part1.D23, HC-SR04_Sensor_1.ECHO
  N7: Part1.D44, LED3.anode
  N8: Part1.D46, LED2.anode
  N9: Part1.D48, LED1.anode
  N10: Part4.M2A, M4.pin_1
  N11: Part4.M2B, M4.pin_2
  N12: Part4.M1B, M3.pin_1
  N13: Part4.M1A, M3.pin_2
  N14: Part4.M3A, M2.pin_2
  N15: Part4.M3B, M2.pin_1
  N16: Part4.M4B, M1.pin_2
  N17: Part4.M4A, M1.pin_1
  GND: Part4.GND, HC-SR04_Sensor_1.GND, Part5.GND, Part6.GND, VCC1.-, R1.Pin_1, R2.Pin_1, R3.Pin_1, Part8.GND, Part7.GND
  N18: Part4.VMOTOR, S1.L2
  VCC: Part4.+5V, HC-SR04_Sensor_1.VCC, Part5.VCC, Part6.VCC, Part7.HV
  N19: Part4.D2, Part5.INT
  N20: Part4.AD5/SCL, Part5.SCL
  N21: Part4.AD4/SDA, Part5.SDA
  N22: VCC1.+, S1.COM
  N23: LED1.cathode, R1.Pin_0
  N24: LED2.cathode, R2.Pin_0
  N25: LED3.cathode, R3.Pin_0
  N26: Part8.HV, Part7.LV

custom parts:
  Adafruit Motor/Stepper/Servo Shield: The original Adafruit Motorshield kit is one of our most beloved kits, which is why we decided to make something even better. We have upgraded the shield kit to make the bestest, easiest way to drive DC and Stepper motors. This shield will make quick work of your next robotics project! We kept the ability to drive up to 4 DC motors or 2 stepper motors, but added many improvements: Instead of a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
  HC-SR04 Ultrasonic Distance Sensor: The HC-SR04 is an ultrasonic distance sensor. It is capable of providing measurement for ranges of 2cm to 400cm. The module operates at 5V.
  BlueSMiRF Silver: Description: The BlueSMiRF Silver is the latest Bluetooth wireless serial cable replacement from SparkFun Electronics! This version of the popular BlueSMiRF uses the RN-42 module which has a bit less range than the RN-41 module used in the BlueSMiRF Gold. These modems work as a serial (RX/TX) pipe. Any serial stream from 2400 to 115200bps can be passed seamlessly from your computer to your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
  Battery: Your standard 2x 18650 battery pack (7,4 Volts)
  Adafruit 4-channel I2C-safe Bi-directional Logic Level Converter: Because the Arduino (and Basic Stamp) are 5V devices, and most modern sensors, displays, flash cards and modes are 3.3V-only, many makers find that they need to perform level shifting/conversion to protect the 3.3V device from 5V. We do have some other handy level shifters in the shop, from the DIP 74LVC245 to the fancy bi-directional TXB0108. However, neither of these are happy to work with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
  Adafruit Pi Cobbler Plus: The Raspberry Pi B+/Pi 2/ Pi 3 has landed on the Maker World like a 40-GPIO pinned, quad-USB ported, credit card sized bomb of DIY joy. And while you can use most of our great Model B accessories by hooking up our downgrade cable, its probably a good time to upgrade your set up and accessorize using all of the Model B+'s / Pi 2's / Pi 3's 40 pins. That's why we now carry the Adafruit Assembled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
